# Fritzing sketch temp, umid, lumin Arduino (saved by Fritzing 0.9.3b)
breadboards: 1

parts:
  Part1 = Arduino Uno (Rev3)
  R1 = PHOTOCELL [package=photocell]
  DHT1 = DHT11 Humitidy and Temperature Sensor
  R2 = Resistor [tolerance=±5% resistance=10 package=THT]

nets:
  N1: Part1.A0, R1.P$1, R2.Pin_1
  N2: Part1.D2, DHT1.VDD
  N3: Part1.5V, R1.P$2, DHT1.DATA
  GND: Part1.GND, DHT1.GND

custom parts:
  DHT11 Humitidy and Temperature Sensor: DHT11 Humidity and Temperature Sensor
